# Fritzing sketch UltraSonicSenseDiagram (saved by Fritzing 0.9.3b)
circuit board: 8.46667cm x 5.64444cm
breadboards: 1

parts:
  Part1 = Arduino Uno (Rev3)
  hc-sr1 = hc-sr04
  LED1 = RGB LED - (4 legs) [package="5 mm [THT]"]
  J1 = Basic Servo

nets:
  N1: Part1.D8, hc-sr1.Trig
  N2: Part1.D9_PWM, hc-sr1.Echo
  GND: Part1.GND, hc-sr1.GND, J1.gnd
  N3: Part1.D4, J1.pulse
  N4: Part1.D5_PWM, LED1.blue_cathode
  N5: Part1.D6_PWM, LED1.green_cathode
  N6: Part1.D7, LED1.red_cathode
  N7: Part1.3V3, LED1.common_anode
  VCC: Part1.5V, hc-sr1.VCC, J1.vcc

// code stored in the sketch: ULTRASONIC-SENSE-PORGECT.fzz.ino
#define echoPin 9
#define trigPin 8
#include <Servo.h>
const int Red = 7;
const int Green = 6;
const int Blue = 5;
Servo myservo; 
int pos = 0;    

long duration; 
long distance; 


void setup() {
  Serial.begin(9600);
  pinMode(echoPin,INPUT);
  pinMode(trigPin,OUTPUT);
  pinMode(Red,OUTPUT);
  pinMode(Green,OUTPUT);
  pinMode(Blue,OUTPUT);
  myservo.attach(4);
}


void loop() {
  
digitalWrite(trigPin,LOW);
  delayMicroseconds(2);
  digitalWrite(trigPin,HIGH);
  delayMicroseconds(10);
  digitalWrite(trigPin,LOW);
  duration = pulseIn(echoPin,HIGH);
  distance = duration/58.2;
  Serial.println(distance);
  delay(50);

if (distance <= 5) {
  digitalWrite(Blue,HIGH);
  for (pos = 0; pos <= 30; pos += 1) { 
    myservo.write(pos);                            
  }
    delay(10000);
  digitalWrite(Blue,LOW);
  for (pos = 30; pos <= 270; pos += 1) { 
    myservo.write(pos);
    digitalWrite(Red,HIGH);
}

}
else {digitalWrite(Blue,LOW)}

}
